# Fritzing sketch Internet Radio ESP32 I2S PCM5102 WS2812 (saved by Fritzing 0.9.4)
circuit board: 20.2231cm x 11.6432cm

parts:
  MH-ET_Live_Minikit_for_ESP1 = MH-ET Live Minikit for ESP32
  PCM5102A_I2S_Stereo_DAC1 = PCM5102A I2S Stereo DAC
  Left_12_LEDs_ring = 12 NeoPixel Ring [part_number=1643]
  M1 = PAM8403 Stereo Amplifier [part_number=HW-104]
  Right_12_LEDs_ring = 12 NeoPixel Ring [part_number=1643]
  SP1 = SPEAKER [package=pcb_mount_speaker]
  SP2 = SPEAKER [package=pcb_mount_speaker]
  R1 = Resistor [tolerance=±5% resistance=10k package=THT]

nets:
  GND: MH-ET_Live_Minikit_for_ESP1.GND, Left_12_LEDs_ring.GND, M1.POWER-, Right_12_LEDs_ring.GND
  N1: MH-ET_Live_Minikit_for_ESP1.IO33, Left_12_LEDs_ring.IN
  N2: MH-ET_Live_Minikit_for_ESP1.TMS, Right_12_LEDs_ring.IN
  VCC: MH-ET_Live_Minikit_for_ESP1.VCC, PCM5102A_I2S_Stereo_DAC1.VIN, R1.Pin_0
  N3: MH-ET_Live_Minikit_for_ESP1.IO4, PCM5102A_I2S_Stereo_DAC1.BCK
  N4: MH-ET_Live_Minikit_for_ESP1.IO0, PCM5102A_I2S_Stereo_DAC1.DIN
  N5: MH-ET_Live_Minikit_for_ESP1.IO2, PCM5102A_I2S_Stereo_DAC1.LRCK
  N6: PCM5102A_I2S_Stereo_DAC1.AGND#5, PCM5102A_I2S_Stereo_DAC1.ROUT, M1.INPUTR
  N7: PCM5102A_I2S_Stereo_DAC1.AGND#7, M1.INPUTG
  N8: PCM5102A_I2S_Stereo_DAC1.LROUT, M1.INPUTL
  N9: PCM5102A_I2S_Stereo_DAC1.SCK, R1.Pin_1
  VDD: Left_12_LEDs_ring.VDD, M1.POWER+, Right_12_LEDs_ring.VDD
  N10: M1.ROUT-, SP1.+
  N11: M1.ROUT+, SP1.-
  N12: M1.LOUT+, SP2.-
  N13: M1.LOUT-, SP2.+

custom parts:
  MH-ET Live Minikit for ESP32: MH-ET Live Minikit for ESP32 ( http://mh.nodebb.com/topic/8/mh-et-live-minikit-for-esp32/2/) PCB footprint is invalid.
  12 NeoPixel Ring: 12 ultra bright smart LED NeoPixels are arranged in a circle with 1.5" (37mm) outer diameter. The rings are 'chainable' - connect the output pin of one to the input pin of another. Use only one microcontroller pin to control as many as you can chain together! Each LED is addressable as the driver chip is inside the LED. Each one has ~18mA constant current drive so the color will be very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
  PAM8403 Stereo Amplifier: PAM8403 stereo amplifier module Descriptive words Links: PAM8403 product datasheet
